# Fritzing sketch ArduinoGiesomat (saved by Fritzing 0.9.3b)
breadboards: 1

parts:
  Bauteil1 = NanoESP
  SN74HC151N = IC, DIP package, 16 pins [chip_label=SN74HC151N]

nets:
  N1: Bauteil1.GND, SN74HC151N.pin8
  N2: Bauteil1.3V3, SN74HC151N.pin16
